# Fritzing sketch PixelArray (saved by Fritzing 1.0.2b)
circuit board: 12.7868cm x 9.40023cm
breadboards: 1

parts:
  R1 = Resistor [tolerance=±5% power=0.25 resistance=220 package=THT]
  R2 = Resistor [tolerance=±5% power=0.25 resistance=220 package=THT]
  R3 = Resistor [tolerance=±5% power=0.25 resistance=220 package=THT]
  R4 = Resistor [tolerance=±5% power=0.25 resistance=220 package=THT]
  R5 = Resistor [tolerance=±5% power=0.25 resistance=220 package=THT]
  R6 = Resistor [tolerance=±5% power=0.25 resistance=220 package=THT]
  R7 = Resistor [tolerance=±5% power=0.25 resistance=220 package=THT]
  R8 = Resistor [tolerance=±5% power=0.25 resistance=220 package=THT]
  S1 = Pushbutton [package="[THT]"]
  J1 = female pin header, 2 pins [form="♀ (female)"]
  U1 = Raspberry Pi Pico
  LED10 = smd LED [color="Red (633nm)" current=0.030 package="0805 [SMD]"]
  LED1 = smd LED [color="Red (633nm)" current=0.030 package="0805 [SMD]"]
  LED2 = smd LED [color="Red (633nm)" current=0.030 package="0805 [SMD]"]
  LED3 = smd LED [color="Red (633nm)" current=0.030 package="0805 [SMD]"]
  LED4 = smd LED [color="Red (633nm)" current=0.030 package="0805 [SMD]"]
  LED5 = smd LED [color="Red (633nm)" current=0.030 package="0805 [SMD]"]
  LED6 = smd LED [color="Red (633nm)" current=0.030 package="0805 [SMD]"]
  LED7 = smd LED [color="Red (633nm)" current=0.030 package="0805 [SMD]"]
  LED8 = smd LED [color="Red (633nm)" current=0.030 package="0805 [SMD]"]
  LED24 = smd LED [color="Red (633nm)" current=0.030 package="0805 [SMD]"]
  LED13 = smd LED [color="Red (633nm)" current=0.030 package="0805 [SMD]"]
  LED9 = smd LED [color="Red (633nm)" current=0.030 package="0805 [SMD]"]
  LED11 = smd LED [color="Red (633nm)" current=0.030 package="0805 [SMD]"]
  LED12 = smd LED [color="Red (633nm)" current=0.030 package="0805 [SMD]"]
  LED14 = smd LED [color="Red (633nm)" current=0.030 package="0805 [SMD]"]
  LED15 = smd LED [color="Red (633nm)" current=0.030 package="0805 [SMD]"]
  LED16 = smd LED [color="Red (633nm)" current=0.030 package="0805 [SMD]"]
  LED23 = smd LED [color="Red (633nm)" current=0.030 package="0805 [SMD]"]
  LED22 = smd LED [color="Red (633nm)" current=0.030 package="0805 [SMD]"]
  LED21 = smd LED [color="Red (633nm)" current=0.030 package="0805 [SMD]"]
  LED20 = smd LED [color="Red (633nm)" current=0.030 package="0805 [SMD]"]
  LED19 = smd LED [color="Red (633nm)" current=0.030 package="0805 [SMD]"]
  LED18 = smd LED [color="Red (633nm)" current=0.030 package="0805 [SMD]"]
  LED17 = smd LED [color="Red (633nm)" current=0.030 package="0805 [SMD]"]
  LED25 = smd LED [color="Red (633nm)" current=0.030 package="0805 [SMD]"]
  LED26 = smd LED [color="Red (633nm)" current=0.030 package="0805 [SMD]"]
  LED27 = smd LED [color="Red (633nm)" current=0.030 package="0805 [SMD]"]
  LED28 = smd LED [color="Red (633nm)" current=0.030 package="0805 [SMD]"]
  LED29 = smd LED [color="Red (633nm)" current=0.030 package="0805 [SMD]"]
  LED30 = smd LED [color="Red (633nm)" current=0.030 package="0805 [SMD]"]
  LED31 = smd LED [color="Red (633nm)" current=0.030 package="0805 [SMD]"]
  LED32 = smd LED [color="Red (633nm)" current=0.030 package="0805 [SMD]"]
  LED33 = smd LED [color="Red (633nm)" current=0.030 package="0805 [SMD]"]
  LED34 = smd LED [color="Red (633nm)" current=0.030 package="0805 [SMD]"]
  LED35 = smd LED [color="Red (633nm)" current=0.030 package="0805 [SMD]"]
  LED36 = smd LED [color="Red (633nm)" current=0.030 package="0805 [SMD]"]
  LED37 = smd LED [color="Red (633nm)" current=0.030 package="0805 [SMD]"]
  LED38 = smd LED [color="Red (633nm)" current=0.030 package="0805 [SMD]"]
  LED39 = smd LED [color="Red (633nm)" current=0.030 package="0805 [SMD]"]
  LED40 = smd LED [color="Red (633nm)" current=0.030 package="0805 [SMD]"]
  LED48 = smd LED [color="Red (633nm)" current=0.030 package="0805 [SMD]"]
  LED47 = smd LED [color="Red (633nm)" current=0.030 package="0805 [SMD]"]
  LED46 = smd LED [color="Red (633nm)" current=0.030 package="0805 [SMD]"]
  LED45 = smd LED [color="Red (633nm)" current=0.030 package="0805 [SMD]"]
  LED44 = smd LED [color="Red (633nm)" current=0.030 package="0805 [SMD]"]
  LED43 = smd LED [color="Red (633nm)" current=0.030 package="0805 [SMD]"]
  LED42 = smd LED [color="Red (633nm)" current=0.030 package="0805 [SMD]"]
  LED41 = smd LED [color="Red (633nm)" current=0.030 package="0805 [SMD]"]
  LED49 = smd LED [color="Red (633nm)" current=0.030 package="0805 [SMD]"]
  LED50 = smd LED [color="Red (633nm)" current=0.030 package="0805 [SMD]"]
  LED51 = smd LED [color="Red (633nm)" current=0.030 package="0805 [SMD]"]
  LED52 = smd LED [color="Red (633nm)" current=0.030 package="0805 [SMD]"]
  LED53 = smd LED [color="Red (633nm)" current=0.030 package="0805 [SMD]"]
  LED54 = smd LED [color="Red (633nm)" current=0.030 package="0805 [SMD]"]
  LED55 = smd LED [color="Red (633nm)" current=0.030 package="0805 [SMD]"]
  LED56 = smd LED [color="Red (633nm)" current=0.030 package="0805 [SMD]"]
  LED57 = smd LED [color="Red (633nm)" current=0.030 package="0805 [SMD]"]
  LED58 = smd LED [color="Red (633nm)" current=0.030 package="0805 [SMD]"]
  LED59 = smd LED [color="Red (633nm)" current=0.030 package="0805 [SMD]"]
  LED60 = smd LED [color="Red (633nm)" current=0.030 package="0805 [SMD]"]
  LED61 = smd LED [color="Red (633nm)" current=0.030 package="0805 [SMD]"]
  LED62 = smd LED [color="Red (633nm)" current=0.030 package="0805 [SMD]"]
  LED63 = smd LED [color="Red (633nm)" current=0.030 package="0805 [SMD]"]
  LED64 = smd LED [color="Red (633nm)" current=0.030 package="0805 [SMD]"]

nets:
  col0: R1.Pin_0, U1.pin_31
  N1: R1.Pin_1, LED1.cathode, LED9.cathode, LED17.cathode, LED25.cathode, LED33.cathode, LED41.cathode, LED49.cathode, LED57.cathode
  col1: R2.Pin_0, U1.pin_29
  N2: R2.Pin_1, LED10.cathode, LED2.cathode, LED18.cathode, LED26.cathode, LED34.cathode, LED42.cathode, LED50.cathode, LED58.cathode
  col2: R3.Pin_0, U1.pin_27
  N3: R3.Pin_1, LED3.cathode, LED11.cathode, LED19.cathode, LED27.cathode, LED35.cathode, LED43.cathode, LED51.cathode, LED59.cathode
  col3: R4.Pin_0, U1.pin_26
  N4: R4.Pin_1, LED4.cathode, LED12.cathode, LED20.cathode, LED28.cathode, LED36.cathode, LED44.cathode, LED52.cathode, LED60.cathode
  col4: R5.Pin_0, U1.pin_25
  N5: R5.Pin_1, LED5.cathode, LED13.cathode, LED21.cathode, LED29.cathode, LED37.cathode, LED45.cathode, LED53.cathode, LED61.cathode
  col5: R6.Pin_0, U1.pin_24
  N6: R6.Pin_1, LED6.cathode, LED14.cathode, LED22.cathode, LED30.cathode, LED38.cathode, LED46.cathode, LED54.cathode, LED62.cathode
  col6: R7.Pin_0, U1.pin_22
  N7: R7.Pin_1, LED7.cathode, LED15.cathode, LED23.cathode, LED31.cathode, LED39.cathode, LED47.cathode, LED55.cathode, LED63.cathode
  col7: R8.Pin_0, U1.pin_21
  N8: R8.Pin_1, LED8.cathode, LED24.cathode, LED16.cathode, LED32.cathode, LED40.cathode, LED48.cathode, LED56.cathode, LED64.cathode
  GND: S1.Pin_2, J1.pin2, U1.pin_3, U1.pin_18, U1.pin_28, U1.pin_38
  N9: S1.Pin_3, S1.Pin_4, U1.pin_30
  VCC: J1.pin1, U1.pin_39
  row7: U1.pin_11, LED57.anode, LED58.anode, LED59.anode, LED60.anode, LED61.anode, LED62.anode, LED63.anode, LED64.anode
  row6: U1.pin_12, LED49.anode, LED50.anode, LED51.anode, LED52.anode, LED53.anode, LED54.anode, LED55.anode, LED56.anode
  row5: U1.pin_14, LED48.anode, LED47.anode, LED46.anode, LED45.anode, LED44.anode, LED43.anode, LED42.anode, LED41.anode
  row4: U1.pin_15, LED33.anode, LED34.anode, LED35.anode, LED36.anode, LED37.anode, LED38.anode, LED39.anode, LED40.anode
  row3: U1.pin_16, LED25.anode, LED26.anode, LED27.anode, LED28.anode, LED29.anode, LED30.anode, LED31.anode, LED32.anode
  row2: U1.pin_17, LED24.anode, LED23.anode, LED22.anode, LED21.anode, LED20.anode, LED19.anode, LED18.anode, LED17.anode
  row1: U1.pin_19, LED10.anode, LED13.anode, LED9.anode, LED11.anode, LED12.anode, LED14.anode, LED15.anode, LED16.anode
  row0: U1.pin_20, LED1.anode, LED2.anode, LED3.anode, LED4.anode, LED5.anode, LED6.anode, LED7.anode, LED8.anode

notes:
  8x8 pixel Matrix

custom parts:
  Raspberry Pi Pico: Raspberry Pi Pico. Based around the RP2040 microcontroller the Pico is a low cost microcontroller device bringing Raspberry Pi quality, cost, and easy of use to the microcontroller space. Jan 2021, Split part in to two versions: tht (this one) and SMD. This one will drill holes for a .1 in header in pcb to allow plugging in the module as well as providing pads to solder the module to the top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
